// Digital circuit main.dig as structural Verilog
module main (
  input  clk,
  input  reset,
  input  [7:0] kb_data,
  input  [12:0] Disp_Addr_RD,
  input  kb_en,
  output [23:0] pc_out,
  output [31:0] mem_din,
  output [31:0] ir_bus,
  output [21:0] ir_offset,
  output [21:0] ir_addr,
  output [5:0] ir_addr_w,
  output [5:0] ir_addr_b,
  output [2:0] wb_sel,
  output [9:0] ir_opcode,
  output [7:0] ctrl_alu_op,
  output [31:0] alu_out,
  output [31:0] reg_w_data,
  output [31:0] p,
  output [23:0] pc_save,
  output [31:0] m_out,
  output [23:0] mem_addr,
  output [2:0] ctrl_w_sel,
  output [31:0] reg_b,
  output [31:0] reg_a,
  output ctrl_reg_we,
  output [5:0] ir_addr_a,
  output [3:0] ir_sel,
  output [31:0] disp_out,
  output [23:0] pc_link
);

  wire and_1_out, bank_en, BANK_SEL, comparator_1_eq, comparator_2_eq, csr_flags, ctrl_alu_pre,
       ctrl_branch_en, ctrl_byte_sel, ctrl_cin_sel, ctrl_cycles, ctrl_flags_we, ctrl_jump_type, ctrl_mem_rd,
       ctrl_mem_wr, ctrl_pc_cond, ctrl_pc_link_WE, ctrl_pc_src, ctrl_shift_op, ctrl_sp_out, HALT_IN,
       mem_rd_out, reg_c, seq_exec, seq_fetch, shift_out;
  wire [1:0] ctrl_mem_sel;
  wire [2:0] ctrl_bus_sel;
  wire [23:0] sp_out;
  wire [31:0] mem_in;

  // program_counter program_counter_1: pin names not known; wires that end beside it: mem_din, alu_out, ctrl_pc_src, ir_offset, reset, ctrl_cycles, csr_flags, ctrl_pc_cond, ctrl_jump_type, ctrl_branch_en, 1'b1, HALT_IN, kb_en, 1'b1, 1'b1, 1'b1, ctrl_pc_link_WE, clk, pc_out, pc_save, seq_fetch, seq_exec, pc_link
  // register register_1: pin names not known; wires that end beside it: ctrl_reg_we, reg_w_data, ir_addr_a, ir_addr_b, ir_addr_w, seq_exec, clk, BANK_SEL, bank_en, reg_a, reg_b, reg_c
  // ir ir_1: pin names not known; wires that end beside it: mem_din, seq_fetch, clk, ir_sel, reg_b, ir_opcode, ir_addr_a, ir_addr_b, ir_addr_w, ir_addr, ir_offset, ir_bus, BANK_SEL
  bus_arbitration bus_arbitration_1 (
    .FETCH(seq_fetch), .IR_ADDR(ir_addr), .MEM_RD_IN(ctrl_mem_rd), .addr_sel(ctrl_bus_sel), .Reg_b(reg_b),
    .Pc_out(pc_out), .SP_out(sp_out), .Alu_in(alu_out), .ADDR_BUS(mem_addr), .MEM_RD_OUT(mem_rd_out));
  store_mux store_mux_1 (
    .reg_a(reg_a), .alu_out(alu_out), .pc_save(pc_save), .reg_b(reg_b), .mem_sel(ctrl_mem_sel),
    .mem_mux(mem_in));
  EEPROMDualPort #(.AddrBits(24), .Bits(32)) eepromdualport_1 (
    .A(mem_addr), .Din(mem_in), .str(ctrl_mem_wr), .C(clk), .ld(mem_rd_out), .D(m_out));
  // microcode microcode_1: pin names not known; wires that end beside it: ir_opcode, ctrl_alu_op, ctrl_alu_pre, ctrl_cin_sel, ctrl_shift_op, ir_sel, bank_en, ctrl_w_sel, ctrl_reg_we, ctrl_flags_we, ctrl_mem_rd, ctrl_mem_wr, ctrl_byte_sel, ctrl_branch_en, ctrl_jump_type, ctrl_pc_src, ctrl_sp_out, ctrl_cycles, ctrl_bus_sel, ctrl_pc_link_WE, ctrl_mem_sel, ctrl_pc_cond
  vga vga_1 (.mem_addr(mem_addr), .mem_din(mem_in), .disp_read_addr(Disp_Addr_RD), .clk(clk), .disp_data_out(disp_out));
  // byte_lane_decoder byte_lane_decoder_1: pin names not known; wires that end beside it: m_out, ctrl_byte_sel, kb_data, mem_din
  Comparator #(.Bits(6)) comparator_1 (.a(6'b000010), .b(ir_addr_w), .eq(comparator_1_eq));  // open: gt, lt
  and and_1 (and_1_out, seq_exec, ctrl_reg_we, comparator_1_eq);
  // shift shift_1: pin names not known; wires that end beside it: reg_a, ctrl_shift_op, ir_bus, shift_out
  // alu_32b_final alu_32b_final_1: pin names not known; wires that end beside it: reg_a, ir_bus, ctrl_alu_op, ctrl_alu_pre, reg_c, ctrl_cin_sel, clk, ctrl_flags_we, alu_out, csr_flags
  // wb_mux wb_mux_1: pin names not known; wires that end beside it: ctrl_w_sel, alu_out, shift_out, pc_save, mem_din, reg_a, ir_bus, csr_flags, {32{1'b0}}, reg_w_data
  Register #(.Bits(32)) register_2 (.D(reg_w_data), .C(clk), .en(and_1_out), .Q(p));
  // sp sp_1: pin names not known; wires that end beside it: ctrl_sp_out, clk, reset, alu_out, seq_exec, sp_out
  and and_2 (HALT_IN, comparator_2_eq, seq_exec);
  Comparator #(.Bits(10)) comparator_2 (.a(10'hff), .b(ir_opcode), .eq(comparator_2_eq));  // open: gt, lt

  assign wb_sel = ctrl_w_sel;

  // Other names for the same wires on the sheet: ctrl_wb_sel[2:0] = ctrl_w_sel; disp_read_addr[12:0] = Disp_Addr_RD;
  //   mem_ram_out[31:0] = m_out

  // Notes on the sheet:
  //   clk: Hz: 10
  //   contents of eepromdualport_1 (hex, n*v repeats v):
  //   0,d400420,400f460,d401850,421420,10c20400,0,400f860,0,c21c30,1031c30
  //   ,1430830,821420,0,1820030,1c20040,3851430,3030030,3430030,2821c30
  //   ,2c21c30,7030042,4001060,8021830,9021040,8421830,9421040,8821830
  //   ,9821040,7821430,7c50830,3c21400,d000000,8c21830,9c21040,4021c30
  //   ,2021430,2421440,482f030,4c30033,5030035,6021400,7441044,5420034
  //   ,5820038,5c21c00,6430000,6c4f340,6834000,28820030,20021430,21420033
  //   ,20c21430,28400020,1c000020,d000000,4*0,deadbeef,a5a5,f0f0f0f0
endmodule
